# Fritzing sketch sonificazione-serra (saved by Fritzing 0.9.3b)
breadboards: 1

parts:
  Componente2 = Arduino Uno (Rev3)
  YL-83_-_Control_Board2 = YL-83 Rain Sensor - Control Board
  YL-83_-_Detection_Board2 = YL-83 Rain Sensor - Detection Board
  R1 = Resistor [tolerance=±5% resistance=10 package=THT]
  Sensor1 = Gas Sensor Breakout Board
  DHT1 = DHT11 Humitidy and Temperature Sensor
  부품2 = FC-28 Soil Hygrometer Module - Probe
  부품3 = FC-28 Soil Hygrometer Module
  Part3 = Ambient Light Sensor (TEMT6000 Breakout Board)

nets:
  N1: Componente2.A0, 부품3.AO
  N2: Componente2.A1, Sensor1.GND
  N3: Componente2.A2, Part3.S
  N4: Componente2.A3, YL-83_-_Control_Board2.AO
  N5: Componente2.D2, R1.Pin_0, R1.Pin_1, DHT1.DATA
  N6: Componente2.D4, YL-83_-_Control_Board2.DO
  N7: Componente2.D5_PWM, 부품3.VCC
  N8: Componente2.D7, YL-83_-_Control_Board2.VCC
  5V: Componente2.5V, Sensor1.5V, DHT1.VDD, Part3.VCC
  GND: Componente2.GND, YL-83_-_Control_Board2.GND, Sensor1.DOUT, DHT1.GND, 부품3.GND, Part3.GND
  N9: YL-83_-_Control_Board2.POS, YL-83_-_Detection_Board2.POS
  N10: YL-83_-_Control_Board2.NEG, YL-83_-_Detection_Board2.NEG
  N11: 부품2.POS, 부품3.POS
  N12: 부품2.NEG, 부품3.NEG

custom parts:
  YL-83 Rain Sensor - Control Board: The YL-83 is a rain sensor that has more resistance when dry and less resistance when wet. The module runs at 5V.
  YL-83 Rain Sensor - Detection Board: The YL-83 is a rain sensor that has more resistance when dry and less resistance when wet. The module runs at 5V.
  Gas Sensor Breakout Board: Gas sensor breakout board. Input voltage is 5V. Sensor output is available in analog and digital.
  DHT11 Humitidy and Temperature Sensor: DHT11 Humidity and Temperature Sensor
  FC-28 Soil Hygrometer Module - Probe: The FC-28 is a soil hygrometer module that uses the Texas Instruments LM393 comparator chip to provide an analog measurement of soil humidity.
  FC-28 Soil Hygrometer Module: The FC-28 is a soil hygrometer module that uses the Texas Instruments LM393 comparator chip to provide an analog measurement of soil humidity. The digital output is high when soil moisture is over a certain threshold, as determined by adjusting the potentiometer.
